// Logisim project question1.circ as structural Verilog: 1 circuit, main circuit main
module main (
  input  S3,
  input  S2,
  input  S1,
  input  S0,
  input  E,
  output Y0,
  output Y1,
  output Y2,
  output Y3,
  output Y4,
  output Y5,
  output Y6,
  output Y7,
  output Y8,
  output Y9,
  output Y10,
  output Y11
);

  wire and_1_out, and_2_out, and_5_out, n2_to_4_decoder_x2_74155_1_p4, n2_to_4_decoder_x2_74155_2_p4,
       n2_to_4_decoder_x2_74155_3_p6, not_1_out, not_2_out, not_3_out, not_4_out;

  not not_1 (not_1_out, S2);
  not not_2 (not_2_out, S3);
  and and_1 (and_1_out, E, S2);
  not not_3 (not_3_out, S3);
  not not_4 (not_4_out, S2);
  // _2_to_4_Decoder__x2___74155 #(.Facing("east")) 2_to_4_decoder_x2_74155_1: pin names not known; wires that end beside it: S0, S1, 1'b0, n2_to_4_decoder_x2_74155_1_p4, 1'b0, 1'b0, Y0, Y1, Y2, Y3
  and and_2 (and_2_out, E, not_1_out);
  and and_3 (n2_to_4_decoder_x2_74155_1_p4, and_2_out, not_2_out);
  // _2_to_4_Decoder__x2___74155 #(.Facing("east")) 2_to_4_decoder_x2_74155_2: pin names not known; wires that end beside it: S0, S1, 1'b0, n2_to_4_decoder_x2_74155_2_p4, 1'b0, 1'b0, Y4, Y5, Y6, Y7
  and and_4 (n2_to_4_decoder_x2_74155_2_p4, and_1_out, not_3_out);
  // _2_to_4_Decoder__x2___74155 #(.Facing("east")) 2_to_4_decoder_x2_74155_3: pin names not known; wires that end beside it: S1, S0, S0, S1, 1'b0, n2_to_4_decoder_x2_74155_3_p6, 1'b0, 1'b0, Y8, Y9, Y10, Y11
  and and_5 (and_5_out, E, not_4_out);
  and and_6 (n2_to_4_decoder_x2_74155_3_p6, and_5_out, S3);
endmodule
